# Fritzing sketch PCA1000X-Breakout (saved by Fritzing 0.8.7b)
circuit board: 5cm x 6cm
breadboards: 1

parts:
  J1 = male pin header, 12 pins [form="♂ (male)"]
  C3 = Ceramic Capacitor [capacitance=0.1µF package="200 mil [THT, multilayer]"]
  J2 = male pin header, 9 pins [form="♂ (male)"]
  J3 = male pin header, 9 pins [form="♂ (male)"]
  J4 = male pin header, 9 pins [form="♂ (male)"]
  C1 = Tantalum Capacitor [capacitance=0.22µF voltage=6.3V package="100 mil [THT, tantalum]"]
  Reset = Pushbutton [package="[THT]"]
  USB = Mini-USB _B Assmann [package=usb-minib]
  U1 = TS2950 Ultra Low Dropout Positive Voltage Regulato [package=to-92]
  J8 = male pin header, 20 pins [form="♂ (male)"]
  J6 = male pin header, 20 pins [form="♂ (male)"]
  J7 = male pin header, 20 pins [form="♂ (male)"]
  J9 = male pin header, 20 pins [form="♂ (male)"]

nets:
  GND: J1.pin1, C1.-, USB.GND, U1.GND, J7.pin3, J9.pin3
  N1: J1.pin2, J9.pin4
  N2: J1.pin4, J9.pin5
  N3: J1.pin5, J9.pin6
  N4: J1.pin6, C3.1
  N5: J1.pin7, J9.pin7
  N6: J1.pin8, J9.pin15
  N7: J1.pin9, J9.pin16
  N8: J1.pin10, J9.pin17
  N9: J1.pin11, J9.pin18
  N10: J1.pin12, C1.+, U1.OUT, J7.pin1, J7.pin2
  N11: C3.0, Reset.Pin_1, Reset.Pin_2, J9.pin13
  N12: J2.pin1, J7.pin4
  N13: J2.pin2, J7.pin5
  N14: J2.pin3, J7.pin6
  N15: J2.pin4, J7.pin7
  N16: J2.pin5, J7.pin15
  N17: J2.pin6, J7.pin16
  N18: J2.pin7, J7.pin17
  N19: J2.pin8, J7.pin18
  N20: J2.pin9, Reset.Pin_3, Reset.Pin_4, J9.pin20
  N21: J3.pin1, J6.pin18
  N22: J3.pin2, J8.pin18
  N23: J3.pin3, J8.pin17
  N24: J3.pin4, J8.pin16
  N25: J3.pin5, J8.pin15
  N26: J3.pin6, J8.pin6
  N27: J3.pin7, J8.pin5
  N28: J3.pin8, J8.pin4
  N29: J3.pin9, J8.pin3
  N30: J4.pin1, J8.pin1, J8.pin2
  N31: J4.pin2, J6.pin3
  N32: J4.pin3, J6.pin4
  N33: J4.pin4, J6.pin5
  N34: J4.pin5, J6.pin6
  N35: J4.pin6, J6.pin7
  N36: J4.pin7, J6.pin15
  N37: J4.pin8, J6.pin16
  N38: J4.pin9, J6.pin17
  N39: USB.VBUS, U1.IN

notes:
  +
  P0.20 18 16 30 28 26 24 GND VTG
  GND25 27 29 17 19 21 23 22/P0.
  GND22 20 18 16 30 28 26 24
  VCC 15 13 11 09 07|RE 05 03 - 01 GND
  github.com/d00616
  | Bootloader/UART |
  PCA1000X Breakout

custom parts:
  Mini-USB _B Assmann: Mini-USB B connector Assmann A-USBB-M5
  TS2950 Ultra Low Dropout Positive Voltage Regulato: TS2950/TS2951 series 150mA Ultra Low Dropout Positive Voltage Regulator
